// Logisim project PROJETO CIRCUITOS DIGITAIS 2.0.circ as structural Verilog: 9 circuits, main circuit main
module main (
  input  [3:0] in_1,
  output a,
  output b,
  output c,
  output d,
  output e,
  output f,
  output g
);

  led_a led_a_1 (.S3(in_1[3]), .S2(in_1[2]), .S1(in_1[1]), .S0(in_1[0]), .out_5(a));
  led_b led_b_1 (.S3(in_1[3]), .S2(in_1[2]), .S1(in_1[1]), .S0(in_1[0]), .out_5(b));
  led_c led_c_1 (.S3(in_1[3]), .S2(in_1[2]), .S1(in_1[1]), .S0(in_1[0]), .out_5(c));
  led_d led_d_1 (.S3(in_1[3]), .S2(in_1[2]), .S1(in_1[1]), .S0(in_1[0]), .out_5(d));
  led_e led_e_1 (.S3(in_1[3]), .S2(in_1[2]), .S1(in_1[1]), .S0(in_1[0]), .out_5(e));
  led_f led_f_1 (.S3(in_1[3]), .S2(in_1[2]), .S1(in_1[1]), .S0(in_1[0]), .out_5(f));
  led_g led_g_1 (.S3(in_1[3]), .S2(in_1[2]), .S1(in_1[1]), .S0(in_1[0]), .out_5(g));
endmodule

// a
module led_a (
  input  S3,
  input  S2,
  input  S1,
  input  S0,
  output out_5
);

  wire and_1_out, and_2_out, and_3_out, and_4_out, and_5_out, and_6_out, and_7_out;

  and and_1 (and_1_out, S1, ~S0);  // AND_Gate
  and and_2 (and_2_out, ~S3, S1);  // AND_Gate
  and and_3 (and_3_out, S3, ~S0);  // AND_Gate
  and and_4 (and_4_out, S3, ~S2, ~S1);  // AND_Gate
  and and_5 (and_5_out, ~S2, ~S1, ~S0);  // AND_Gate
  and and_6 (and_6_out, ~S3, S2, S0);  // AND_Gate
  and and_7 (and_7_out, S3, S2, S1);
  or or_1 (out_5, and_1_out, and_2_out, and_3_out, and_4_out, and_5_out, and_6_out, and_7_out);
endmodule

// b
module led_b (
  input  S3,
  input  S2,
  input  S1,
  input  S0,
  output out_5
);

  wire and_1_out, and_2_out, and_3_out, and_4_out, and_5_out, and_6_out;

  and and_1 (and_1_out, ~S3, ~S2);  // AND_Gate
  and and_2 (and_2_out, ~S2, ~S1);  // AND_Gate
  and and_3 (and_3_out, ~S3, ~S1, ~S0);  // AND_Gate
  and and_4 (and_4_out, S3, ~S1, S0);  // AND_Gate
  and and_5 (and_5_out, ~S3, S1, S0);  // AND_Gate
  and and_6 (and_6_out, ~S2, ~S0);  // AND_Gate
  or or_1 (out_5, and_1_out, and_2_out, and_3_out, and_4_out, and_5_out, and_6_out);
endmodule

// c
module led_c (
  input  S3,
  input  S2,
  input  S1,
  input  S0,
  output out_5
);

  wire and_1_out, and_2_out, and_3_out, and_4_out, and_5_out;

  and and_1 (and_1_out, S3, ~S2);  // AND_Gate
  and and_2 (and_2_out, ~S3, S2);  // AND_Gate
  and and_3 (and_3_out, ~S1, S0);  // AND_Gate
  and and_4 (and_4_out, ~S3, ~S1, ~S0);  // AND_Gate
  and and_5 (and_5_out, ~S3, S1, S0);  // AND_Gate
  or or_1 (out_5, and_1_out, and_2_out, and_3_out, and_4_out, and_5_out);
endmodule

// d
module led_d (
  input  S3,
  input  S2,
  input  S1,
  input  S0,
  output out_5
);

  wire and_1_out, and_2_out, and_3_out, and_4_out, and_5_out;

  and and_1 (and_1_out, ~S2, S1, S0);  // AND_Gate
  and and_2 (and_2_out, ~S3, S1, ~S0);  // AND_Gate
  and and_3 (and_3_out, S2, ~S1, S0);  // AND_Gate
  and and_4 (and_4_out, S3, S2, ~S0);  // AND_Gate
  and and_5 (and_5_out, ~S2, ~S1, ~S0);  // AND_Gate
  or or_1 (out_5, and_1_out, and_2_out, and_3_out, and_4_out, and_5_out);
endmodule

// e
module led_e (
  input  S3,
  input  S2,
  input  S1,
  input  S0,
  output out_5
);

  wire and_1_out, and_2_out, and_3_out, and_4_out;

  and and_1 (and_1_out, S3, S2);
  and and_2 (and_2_out, S1, ~S0);  // AND_Gate
  and and_3 (and_3_out, ~S2, ~S1, ~S0);  // AND_Gate
  and and_4 (and_4_out, S3, S1, S0);
  or or_1 (out_5, and_1_out, and_2_out, and_3_out, and_4_out);
endmodule

// f
module led_f (
  input  S3,
  input  S2,
  input  S1,
  input  S0,
  output out_5
);

  wire and_1_out, and_2_out, and_3_out, and_4_out, and_5_out;

  and and_1 (and_1_out, S3, ~S2);  // AND_Gate
  and and_2 (and_2_out, ~S1, ~S0);  // AND_Gate
  and and_3 (and_3_out, S2, S1, ~S0);  // AND_Gate
  and and_4 (and_4_out, S3, S1, S0);
  and and_5 (and_5_out, ~S3, S2, ~S1);  // AND_Gate
  or or_1 (out_5, and_1_out, and_2_out, and_3_out, and_4_out, and_5_out);
endmodule

// g
module led_g (
  input  S3,
  input  S2,
  input  S1,
  input  S0,
  output out_5
);

  wire and_1_out, and_2_out, and_3_out, and_4_out, and_5_out;

  and and_1 (and_1_out, S1, ~S0);  // AND_Gate
  and and_2 (and_2_out, S3, ~S2);  // AND_Gate
  and and_3 (and_3_out, ~S3, S2, ~S1);  // AND_Gate
  and and_4 (and_4_out, S3, S2, S0);
  and and_5 (and_5_out, ~S2, S1, S0);  // AND_Gate
  or or_1 (out_5, and_1_out, and_2_out, and_3_out, and_4_out, and_5_out);
endmodule

module leds (
  input  [3:0] in_1
);

  wire main_1_a, main_1_b, main_1_c, main_1_d, main_1_e, main_1_f, main_1_g;

  main main_1 (
    .in_1(in_1), .a(main_1_a), .b(main_1_b), .c(main_1_c), .d(main_1_d), .e(main_1_e), .f(main_1_f),
    .g(main_1_g));
  _7_Segment_Display u_7_segment_display_1 (
    .g(main_1_g), .f(main_1_f), .a(main_1_a), .b(main_1_b), .e(main_1_e), .d(main_1_d), .c(main_1_c));  // open: dp
  // DisplayDecoder displaydecoder_1: pin names not known
endmodule
