// Logisim project PROJETO CIRCUITOS DIGITAIS 22.0 (1).circ as structural Verilog: 25 circuits, main circuit main
module main (
  input  [3:0] in_1,
  output a,
  output b,
  output c,
  output d,
  output e,
  output f,
  output g
);

  led_a led_a_1 (.S3(in_1[3]), .S2(in_1[2]), .S1(in_1[1]), .S0(in_1[0]), .out_5(a));
  led_b led_b_1 (.S3(in_1[3]), .S2(in_1[2]), .S1(in_1[1]), .S0(in_1[0]), .out_5(b));
  led_c led_c_1 (.S3(in_1[3]), .S2(in_1[2]), .S1(in_1[1]), .S0(in_1[0]), .out_5(c));
  led_d led_d_1 (.S3(in_1[3]), .S2(in_1[2]), .S1(in_1[1]), .S0(in_1[0]), .out_5(d));
  led_e led_e_1 (.S3(in_1[3]), .S2(in_1[2]), .S1(in_1[1]), .S0(in_1[0]), .out_5(e));
  led_f led_f_1 (.S3(in_1[3]), .S2(in_1[2]), .S1(in_1[1]), .S0(in_1[0]), .out_5(f));
  led_g led_g_1 (.S3(in_1[3]), .S2(in_1[2]), .S1(in_1[1]), .S0(in_1[0]), .out_5(g));

  // Notes on the sheet:
  //   Jogo completo em "macro".
endmodule

// a
module led_a (
  input  S3,
  input  S2,
  input  S1,
  input  S0,
  output out_5
);

  wire and_1_out, and_2_out, and_3_out, and_4_out, and_5_out, and_6_out, and_7_out;

  and and_1 (and_1_out, S1, ~S0);  // AND_Gate
  and and_2 (and_2_out, ~S3, S1);  // AND_Gate
  and and_3 (and_3_out, S3, ~S0);  // AND_Gate
  and and_4 (and_4_out, S3, ~S2, ~S1);  // AND_Gate
  and and_5 (and_5_out, ~S2, ~S1, ~S0);  // AND_Gate
  and and_6 (and_6_out, ~S3, S2, S0);  // AND_Gate
  and and_7 (and_7_out, S3, S2, S1);
  or or_1 (out_5, and_1_out, and_2_out, and_3_out, and_4_out, and_5_out, and_6_out, and_7_out);
endmodule

// b
module led_b (
  input  S3,
  input  S2,
  input  S1,
  input  S0,
  output out_5
);

  wire and_1_out, and_2_out, and_3_out, and_4_out, and_5_out, and_6_out;

  and and_1 (and_1_out, ~S3, ~S2);  // AND_Gate
  and and_2 (and_2_out, ~S2, ~S1);  // AND_Gate
  and and_3 (and_3_out, ~S3, ~S1, ~S0);  // AND_Gate
  and and_4 (and_4_out, S3, ~S1, S0);  // AND_Gate
  and and_5 (and_5_out, ~S3, S1, S0);  // AND_Gate
  and and_6 (and_6_out, ~S2, ~S0);  // AND_Gate
  or or_1 (out_5, and_1_out, and_2_out, and_3_out, and_4_out, and_5_out, and_6_out);
endmodule

// c
module led_c (
  input  S3,
  input  S2,
  input  S1,
  input  S0,
  output out_5
);

  wire and_1_out, and_2_out, and_3_out, and_4_out, and_5_out;

  and and_1 (and_1_out, S3, ~S2);  // AND_Gate
  and and_2 (and_2_out, ~S3, S2);  // AND_Gate
  and and_3 (and_3_out, ~S1, S0);  // AND_Gate
  and and_4 (and_4_out, ~S3, ~S1, ~S0);  // AND_Gate
  and and_5 (and_5_out, ~S3, S1, S0);  // AND_Gate
  or or_1 (out_5, and_1_out, and_2_out, and_3_out, and_4_out, and_5_out);
endmodule

// d
module led_d (
  input  S3,
  input  S2,
  input  S1,
  input  S0,
  output out_5
);

  wire and_1_out, and_2_out, and_3_out, and_4_out, and_5_out;

  and and_1 (and_1_out, ~S2, S1, S0);  // AND_Gate
  and and_2 (and_2_out, ~S3, S1, ~S0);  // AND_Gate
  and and_3 (and_3_out, S2, ~S1, S0);  // AND_Gate
  and and_4 (and_4_out, S3, S2, ~S0);  // AND_Gate
  and and_5 (and_5_out, ~S2, ~S1, ~S0);  // AND_Gate
  or or_1 (out_5, and_1_out, and_2_out, and_3_out, and_4_out, and_5_out);
endmodule

// e
module led_e (
  input  S3,
  input  S2,
  input  S1,
  input  S0,
  output out_5
);

  wire and_1_out, and_2_out, and_3_out, and_4_out;

  and and_1 (and_1_out, S3, S2);
  and and_2 (and_2_out, S1, ~S0);  // AND_Gate
  and and_3 (and_3_out, ~S2, ~S1, ~S0);  // AND_Gate
  and and_4 (and_4_out, S3, S1, S0);
  or or_1 (out_5, and_1_out, and_2_out, and_3_out, and_4_out);
endmodule

// f
module led_f (
  input  S3,
  input  S2,
  input  S1,
  input  S0,
  output out_5
);

  wire and_1_out, and_2_out, and_3_out, and_4_out, and_5_out;

  and and_1 (and_1_out, S3, ~S2);  // AND_Gate
  and and_2 (and_2_out, ~S1, ~S0);  // AND_Gate
  and and_3 (and_3_out, S2, S1, ~S0);  // AND_Gate
  and and_4 (and_4_out, S3, S1, S0);
  and and_5 (and_5_out, ~S3, S2, ~S1);  // AND_Gate
  or or_1 (out_5, and_1_out, and_2_out, and_3_out, and_4_out, and_5_out);
endmodule

// g
module led_g (
  input  S3,
  input  S2,
  input  S1,
  input  S0,
  output out_5
);

  wire and_1_out, and_2_out, and_3_out, and_4_out, and_5_out;

  and and_1 (and_1_out, S1, ~S0);  // AND_Gate
  and and_2 (and_2_out, S3, ~S2);  // AND_Gate
  and and_3 (and_3_out, ~S3, S2, ~S1);  // AND_Gate
  and and_4 (and_4_out, S3, S2, S0);
  and and_5 (and_5_out, ~S2, S1, S0);  // AND_Gate
  or or_1 (out_5, and_1_out, and_2_out, and_3_out, and_4_out, and_5_out);
endmodule

module leds (
  input  in_1,
  input  in_2,
  input  [3:0] in_3
);

  wire main_1_a, main_1_b, main_1_c, main_1_d, main_1_e, main_1_f, main_1_g;
  wire [3:0] random_1_out;

  Random #(.width(4)) random_1 (.next(in_1), .out(random_1_out), .clr(in_2));  // open: clk
  main main_1 (
    .a(main_1_a), .b(main_1_b), .c(main_1_c), .d(main_1_d), .e(main_1_e), .f(main_1_f), .g(main_1_g),
    .in_1(in_3));
  _7_Segment_Display u_7_segment_display_1 (
    .g(main_1_g), .f(main_1_f), .a(main_1_a), .b(main_1_b), .e(main_1_e), .d(main_1_d), .c(main_1_c));  // open: dp
endmodule

module subtrator (
  input  a,
  input  b,
  output s,
  output cout
);

  xor xor_1 (s, a, b);
  and and_1 (cout, ~a, b);  // AND_Gate
endmodule

module subtratorcompleto (
  input  a,
  input  b,
  input  cin,
  output s,
  output cout
);

  wire and_1_out, and_2_out, and_3_out, and_4_out, and_5_out, and_6_out, and_7_out;

  and and_1 (and_1_out, cin, ~b, ~a);  // AND_Gate
  and and_2 (and_2_out, ~cin, b, ~a);  // AND_Gate
  and and_3 (and_3_out, cin, b, a);
  and and_4 (and_4_out, ~cin, ~b, a);  // AND_Gate
  and and_5 (and_5_out, cin, ~a);  // AND_Gate
  and and_6 (and_6_out, b, ~a);  // AND_Gate
  and and_7 (and_7_out, cin, b);
  or or_1 (s, and_1_out, and_2_out, and_3_out, and_4_out);
  or or_2 (cout, and_5_out, and_6_out, and_7_out);
endmodule

module multiplexador (
  input  [3:0] E0,
  input  [3:0] E1,
  input  in_3,
  output [3:0] out_4
);

  wire [3:0] and_1_out, and_2_out, bit_extender_1_out;

  assign bit_extender_1_out = {{3{in_3}}, in_3};  // Bit_Extender bit_extender_1
  assign and_1_out = E0 & ~bit_extender_1_out;  // AND_Gate and_1, 4 bits wide
  assign and_2_out = E1 & bit_extender_1_out;  // AND_Gate and_2, 4 bits wide
  assign out_4 = and_1_out | and_2_out;  // OR_Gate or_1, 4 bits wide
endmodule

module somador1 (
  input  a,
  input  b,
  output cout,
  output s
);

  and and_1 (cout, a, b);
  xor xor_1 (s, a, b);
endmodule

module somador_2 (
  input  a,
  input  b,
  input  cin,
  output cout,
  output s
);

  wire and_1_out, and_2_out, and_3_out, xor_1_out;

  and and_1 (and_1_out, b, a);
  and and_2 (and_2_out, cin, b);
  and and_3 (and_3_out, cin, a);
  xor xor_1 (xor_1_out, a, b);
  or or_1 (cout, and_1_out, and_2_out, and_3_out);
  xor xor_2 (s, xor_1_out, cin);
endmodule

// +
module juntatudosoma (
  input  [3:0] b,
  input  [3:0] a,
  output out_3,
  output [3:0] somador
);

  wire somador1_1_cout, somador_2_2_cout, somador_2_3_cout;

  somador_2 somador_2_1 (.cout(out_3), .s(somador[3]), .a(a[3]), .b(b[3]), .cin(somador_2_2_cout));
  somador_2 somador_2_2 (.cout(somador_2_2_cout), .s(somador[2]), .a(a[2]), .b(b[2]), .cin(somador_2_3_cout));
  somador_2 somador_2_3 (.cout(somador_2_3_cout), .s(somador[1]), .a(a[1]), .b(b[1]), .cin(somador1_1_cout));
  somador1 somador1_1 (.cout(somador1_1_cout), .s(somador[0]), .a(a[0]), .b(b[0]));
endmodule

// |
module complemento_de_2 (
  input  [3:0] a,
  output [3:0] out_2,
  output out_3
);

  wire [3:0] not_1_out;

  assign not_1_out = ~a;  // NOT_Gate not_1, 4 bits wide
  juntatudosoma juntatudosoma_1 (.somador(out_2), .out_3(out_3), .b(not_1_out), .a(4'b0001));
endmodule

module somador (
  input  [3:0] a,
  input  [3:0] b,
  input  in_3,
  output [3:0] out_4
);

  wire [3:0] complemento_de_2_1_out_2, complemento_de_2_2_out_2, juntatudosoma_1_somador,
       juntatudosoma_2_somador;

  complemento_de_2 complemento_de_2_1 (.a(b), .out_2(complemento_de_2_1_out_2));  // open: out_3
  complemento_de_2 complemento_de_2_2 (.a(a), .out_2(complemento_de_2_2_out_2));  // open: out_3
  juntatudosoma juntatudosoma_1 (
    .somador(juntatudosoma_1_somador), .b(a), .a(complemento_de_2_1_out_2));  // open: out_3
  juntatudosoma juntatudosoma_2 (
    .somador(juntatudosoma_2_somador), .b(complemento_de_2_2_out_2), .a(b));  // open: out_3
  multiplexador multiplexador_1 (
    .E0(juntatudosoma_1_somador), .E1(juntatudosoma_2_somador), .in_3(in_3), .out_4(out_4));
endmodule

module comparador_de_magnitude (
  input  A3,
  input  B3,
  input  A2,
  input  B2,
  input  A1,
  input  B1,
  input  A0,
  input  B0,
  output a_b,
  output a_b_2,
  output a_b_3
);

  wire and_1_out, and_2_out, and_3_out, and_4_out, xnor_1_out, xnor_2_out, xnor_3_out, xnor_4_out;

  xnor xnor_1 (xnor_1_out, A3, B3);
  xnor xnor_2 (xnor_2_out, A2, B2);
  xnor xnor_3 (xnor_3_out, A1, B1);
  xnor xnor_4 (xnor_4_out, A0, B0);
  and and_1 (and_1_out, A3, ~B3);  // AND_Gate
  and and_2 (and_2_out, xnor_1_out, A2, ~B2);  // AND_Gate
  and and_3 (and_3_out, xnor_1_out, xnor_2_out, A1, ~B1);  // AND_Gate
  and and_4 (and_4_out, xnor_3_out, xnor_2_out, xnor_1_out, A0, ~B0);  // AND_Gate
  and and_5 (a_b, xnor_1_out, xnor_2_out, xnor_3_out, xnor_4_out);
  or or_1 (a_b_2, and_1_out, and_2_out, and_3_out, and_4_out);
  nor nor_1 (a_b_3, a_b, a_b_2);
endmodule

module comparador_de_magnitude_2_0 (
  input  a3,
  input  b3,
  input  a2,
  input  b2,
  input  a1,
  input  b1,
  input  a0,
  input  b0,
  output a_b,
  output a_b_2,
  output a_b_3
);

  wire and_2_out, and_3_out, and_4_out, and_5_out, and_6_out, and_7_out, and_8_out, and_9_out, xnor_1_out,
       xnor_2_out, xnor_3_out, xnor_4_out;

  xnor xnor_1 (xnor_1_out, a3, b3);
  xnor xnor_2 (xnor_2_out, a2, b2);
  xnor xnor_3 (xnor_3_out, a1, b1);
  xnor xnor_4 (xnor_4_out, a0, b0);
  and and_1 (a_b, xnor_1_out, xnor_3_out, xnor_2_out, xnor_4_out);
  and and_2 (and_2_out, a3, ~b3);  // AND_Gate
  and and_3 (and_3_out, a2, xnor_1_out, ~b2);  // AND_Gate
  and and_4 (and_4_out, a1, xnor_1_out, xnor_3_out, ~b1);  // AND_Gate
  and and_5 (and_5_out, a0, xnor_1_out, xnor_3_out, xnor_2_out, ~b0);  // AND_Gate
  or or_1 (a_b_3, and_2_out, and_3_out, and_4_out, and_5_out);
  and and_6 (and_6_out, ~a3, b3);  // AND_Gate
  and and_7 (and_7_out, ~a2, xnor_1_out, b2);  // AND_Gate
  and and_8 (and_8_out, ~a1, xnor_1_out, xnor_3_out, b1);  // AND_Gate
  and and_9 (and_9_out, ~a0, xnor_1_out, xnor_3_out, xnor_2_out, b0);  // AND_Gate
  or or_2 (a_b_2, and_6_out, and_7_out, and_8_out, and_9_out);
endmodule

module comparador_otimizado (
  input  [3:0] b,
  input  [3:0] a,
  output out_3,
  output out_4,
  output out_5
);

  comparador_de_magnitude comparador_de_magnitude_1 (
    .A3(a[3]), .B3(b[3]), .A2(a[2]), .B2(b[2]), .A1(a[1]), .B1(b[1]), .A0(a[0]), .B0(b[0]), .a_b(out_3),
    .a_b_2(out_4), .a_b_3(out_5));
endmodule

module \diferença  (
  input  [3:0] a,
  input  [3:0] b,
  output [3:0] out_3
);

  wire comparador_de_magnitude_out_4;

  Hex_Digit_Display hex_digit_display_1 (.value(a));  // open: dp
  Hex_Digit_Display hex_digit_display_2 (.value(b));  // open: dp
  comparador_otimizado comparador_de_magnitude (
    .out_4(comparador_de_magnitude_out_4), .b(b), .a(a));  // open: out_3, out_5
  somador somador_plus (.out_4(out_3), .a(b), .b(a), .in_3(comparador_de_magnitude_out_4));
  Hex_Digit_Display hex_digit_display_3 (.value(out_3));  // open: dp
endmodule

module guess_the_number (
  input  in_1,
  input  in_2,
  input  [3:0] palpite,
  output acertou,
  output [7:0] vermelho,
  output [7:0] azul
);

  wire comparador_2_out_3;
  wire [3:0] \diferença_out_3 , random_1_out;
  wire [7:0] bit_extender_1_out, cores_out_2, cores_out_3;

  assign bit_extender_1_out = {{7{in_1}}, in_1};  // Bit_Extender bit_extender_1
  Random #(.width(4)) random_1 (.clk(in_2), .out(random_1_out));  // open: next, clr
  comparador_otimizado_2 comparador_2 (.b(random_1_out), .a(palpite), .out_3(comparador_2_out_3));
  assign vermelho = bit_extender_1_out & cores_out_2;  // AND_Gate and_1, 8 bits wide
  \diferença  \diferença  (.a(random_1_out), .b(palpite), .out_3(\diferença_out_3 ));
  cores cores (.out_2(cores_out_2), .out_3(cores_out_3), .in_1(\diferença_out_3 ));
  assign azul = cores_out_3 & bit_extender_1_out;  // AND_Gate and_2, 8 bits wide
  and and_3 (acertou, in_1, comparador_2_out_3);
endmodule

module cores (
  input  [3:0] in_1,
  output [7:0] out_2,
  output [7:0] out_3
);

  assign out_2[7:4] = ~in_1;  // NOT_Gate not_1, 4 bits wide

  assign out_2[3:0] = 4'b1111;
  assign out_3 = {in_1, 4'b1111};
endmodule

module comparador_otimizado_2 (
  input  [3:0] b,
  input  [3:0] a,
  output out_3
);

  comparador_de_magnitude_2_0 comparador_de_magnitude_2_0_1 (
    .a3(a[3]), .b3(a[2]), .a2(a[1]), .b2(a[0]), .a1(b[3]), .b1(b[2]), .a0(b[1]), .a_b_3(out_3), .b0(b[0]));  // open: a_b, a_b_2
endmodule

module macro (
  input  [3:0] palpite,
  input  confirmar
);

  wire guess_the_number_1_acertou, main_1_a, main_1_b, main_1_c, main_1_d, main_1_e, main_1_f, main_1_g,
       rgbled_1_p1;

  guess_the_number guess_the_number_1 (
    .in_1(confirmar), .palpite(palpite), .acertou(guess_the_number_1_acertou), .in_2(confirmar));  // open: vermelho, azul
  // RGBLed #(.multibit("true")) rgbled_1: pin names not known; wires that end beside it: rgbled_1_p1
  Button button_1 (.out(rgbled_1_p1));
  LED led_1 (.in(guess_the_number_1_acertou));
  main main_1 (
    .a(main_1_a), .b(main_1_b), .c(main_1_c), .d(main_1_d), .e(main_1_e), .f(main_1_f), .g(main_1_g),
    .in_1(palpite));
  _7_Segment_Display u_7_segment_display_1 (
    .g(main_1_g), .f(main_1_f), .a(main_1_a), .b(main_1_b), .e(main_1_e), .d(main_1_d), .c(main_1_c));  // open: dp

  // Notes on the sheet:
  //   🔄
  //   🔄
  //   🔄
  //   ☀
  //   ❄
  //   Guess
  //   The Number
  //   🎲
  //   ✔
  //   Decoder
  //   💫
  //   A=10    $b=11$C=12$d=13$E=14$F=15     
endmodule
