// Logisim project comparador de magnitude.circ as structural Verilog: 1 circuit, main circuit main
module main (
  input  a3,
  input  b3,
  input  a2,
  input  b2,
  input  a1,
  input  b1,
  input  a0,
  input  b0,
  output a_b,
  output a_b_2,
  output a_b_3
);

  wire and_2_out, and_3_out, and_4_out, and_5_out, and_6_out, and_7_out, and_8_out, and_9_out, xnor_1_out,
       xnor_2_out, xnor_3_out, xnor_4_out;

  xnor xnor_1 (xnor_1_out, a3, b3);
  xnor xnor_2 (xnor_2_out, a2, b2);
  xnor xnor_3 (xnor_3_out, a1, b1);
  xnor xnor_4 (xnor_4_out, a0, b0);
  and and_1 (a_b, xnor_1_out, xnor_3_out, xnor_2_out, xnor_4_out);
  and and_2 (and_2_out, a3, ~b3);  // AND_Gate
  and and_3 (and_3_out, a2, xnor_1_out, ~b2);  // AND_Gate
  and and_4 (and_4_out, a1, xnor_1_out, xnor_3_out, ~b1);  // AND_Gate
  and and_5 (and_5_out, a0, xnor_1_out, xnor_3_out, xnor_2_out, ~b0);  // AND_Gate
  or or_1 (a_b_3, and_2_out, and_3_out, and_4_out, and_5_out);
  and and_6 (and_6_out, ~a3, b3);  // AND_Gate
  and and_7 (and_7_out, ~a2, xnor_1_out, b2);  // AND_Gate
  and and_8 (and_8_out, ~a1, xnor_1_out, xnor_3_out, b1);  // AND_Gate
  and and_9 (and_9_out, ~a0, xnor_1_out, xnor_3_out, xnor_2_out, b0);  // AND_Gate
  or or_2 (a_b_2, and_6_out, and_7_out, and_8_out, and_9_out);
endmodule
